# Fritzing sketch electronical_drawing (saved by Fritzing 0.9.3b)

parts:
  U1 = ESP8266 NodeMCU LoLin module
  U3 = WS2812 RGB LED strip
  R1 = Resistor [tolerance=±5% resistance=330 package=THT]
  SP1 = SPEAKER [package=pcb_mount_speaker]
  Part1 = InvenSense MPU6050
  U4 = WS2812 RGB LED strip
  LED1 = LEDs [package=led10mm]
  S2 = Round Pushbutton
  R2 = Resistor [tolerance=±5% resistance=68k package=THT]
  U2 = LIPO-1000mAh [package=lipo-1000]
  M1 = TP4056 Module [part_number=HW-107]
  MOD1 = MT3608 Boost No usb
  DFRobot_DFPlayer_Mini1 = DFRobot DFPlayer Mini [part_number=DFR0299]
  R3 = Resistor [tolerance=±5% resistance=330 package=THT]
  R5 = Resistor [tolerance=±5% resistance=330 package=THT]

nets:
  N1: U1.D0, R1.Pin_1, R5.Pin_1
  N2: U1.D1, DFRobot_DFPlayer_Mini1.TX
  N3: U1.D2, R3.Pin_0
  N4: U1.D3, S2.leg0
  N5: U1.D4, LED1.C
  3V3: U1.3V3, Part1.VCC
  N6: U1.D5, Part1.SCL
  N7: U1.D6, Part1.SDA
  GND: U1.GND, U3.GND, Part1.GND, U4.GND, S2.leg1, M1.OUT-#1, MOD1.IN_(-), MOD1.OUT_(-), DFRobot_DFPlayer_Mini1.GND-2
  VCC: U1.Vin, U3.VCC, U4.VCC, MOD1.OUT_(+)
  N8: U1.A0, R2.Pin_0
  N9: U3.DIN, R5.Pin_0
  N10: R1.Pin_0, U4.DIN
  N11: SP1.+, DFRobot_DFPlayer_Mini1.SPK_2
  N12: SP1.-, DFRobot_DFPlayer_Mini1.SPK_1
  N13: LED1.A, DFRobot_DFPlayer_Mini1.VCC
  N14: R2.Pin_1, U2.+, M1.BAT+
  N15: U2.-, M1.BAT-
  N16: M1.OUT-#4, MOD1.IN_(+)
  N17: DFRobot_DFPlayer_Mini1.RX, R3.Pin_1

notes:
  This LED is representing the button backlight as I have not found a specific component for this button I bought

custom parts:
  ESP8266 NodeMCU LoLin module: ESP8266 based NodeMCU
  WS2812 RGB LED strip: WS2812 strip
  TP4056 Module: TP4056 Lithium Battery Charge Management Module Links: TP4056 website
  MT3608 Boost No usb: Chip- MT3608 / B6289 DC to DC step up, power booster module. With adjustable output voltage. Current- 2A . || Input voltage- 2V-24V || Output voltage- 5V-28V Input interface- Inversed polarity- NO. || Led indicator- No.
